// Logisim project RV32I.circ as structural Verilog
module ALU_1bit (
  input  Ainvert,
  input  Cin,
  input  A,
  input  Less,
  input  B,
  input  [1:0] Op,
  input  Binvert,
  output Result,
  output Cout
);

  wire adder_1_out, and_1_out, multiplexer_1_out, multiplexer_2_out, not_1_out, not_2_out, or_1_out;

  not not_1 (not_1_out, A);
  Multiplexer multiplexer_1 (.in0(A), .in1(not_1_out), .out(multiplexer_1_out), .sel(Ainvert));
  Multiplexer multiplexer_2 (.in0(B), .in1(not_2_out), .out(multiplexer_2_out), .sel(Binvert));
  not not_2 (not_2_out, B);
  and and_1 (and_1_out, multiplexer_1_out, multiplexer_2_out);
  or or_1 (or_1_out, multiplexer_1_out, multiplexer_2_out);
  Adder #(.width(1)) adder_1 (.a(multiplexer_1_out), .b(multiplexer_2_out), .out(adder_1_out), .cin(Cin), .cout(Cout));
  Multiplexer #(.select(2)) multiplexer_3 (
    .in0(and_1_out), .in1(or_1_out), .in2(adder_1_out), .in3(Less), .out(Result), .sel(Op));
endmodule

module ALU_32bit (
  input  [31:0] dataA,
  input  [31:0] dataB,
  input  [3:0] sel,
  output [31:0] result
);

  wire comparator_1_lt;
  wire [31:0] addOut, sllOut, sltOut, subOut;

  Adder #(.width(32)) adder_1 (.a(dataA), .b(dataB), .out(addOut));  // open: cin, cout
  Subtractor #(.width(32)) subtractor_1 (.a(dataA), .b(dataB), .out(subOut));  // open: bin, bout
  Shifter #(.width(32)) shifter_1 (.in(dataA), .\dist (dataB[4:0]), .out(sllOut));
  Comparator #(.width(32)) comparator_1 (.a(dataA), .b(dataB), .lt(comparator_1_lt));  // open: gt, eq
  assign sltOut = {{31{1'b0}}, comparator_1_lt};  // Bit_Extender bit_extender_1

  // Other names for the same wires on the sheet: dataA_t[31:0] = dataA; dataB_t[31:0] = dataB;
  //   dataBL5_t[4:0] = dataB[4:0]; result_t[31:0] = result; sel_t[3:0] = sel
endmodule

module ALU_MSB_1bit (
  input  Ainvert,
  input  Cin,
  input  A,
  input  Less,
  input  B,
  input  [1:0] Op,
  input  Binvert,
  output Result,
  output Cout,
  output Set
);

  wire and_1_out, multiplexer_1_out, multiplexer_2_out, not_1_out, not_2_out, or_1_out;

  not not_1 (not_1_out, A);
  Multiplexer multiplexer_1 (.in0(A), .in1(not_1_out), .out(multiplexer_1_out), .sel(Ainvert));
  Multiplexer multiplexer_2 (.in0(B), .in1(not_2_out), .out(multiplexer_2_out), .sel(Binvert));
  not not_2 (not_2_out, B);
  and and_1 (and_1_out, multiplexer_1_out, multiplexer_2_out);
  or or_1 (or_1_out, multiplexer_1_out, multiplexer_2_out);
  Adder #(.width(1)) adder_1 (.a(multiplexer_1_out), .b(multiplexer_2_out), .out(Set), .cin(Cin), .cout(Cout));
  Multiplexer #(.select(2)) multiplexer_3 (
    .in0(and_1_out), .in1(or_1_out), .in2(Set), .in3(Less), .out(Result), .sel(Op));
endmodule
